// Digital circuit ALU-FINAL.dig as structural Verilog
module ALU_FINAL (
  input  [7:0] A,
  input  [7:0] B,
  input  [2:0] Sel___AC,
  input  [1:0] Sel___MQ,
  output [7:0] AC,
  output [7:0] MQ
);

  wire [7:0] LSB, MSB, NAND, Quociente, Resto, Shift_direita, Shift_esquerda, Soma, \Subtração , XOR;

  Subtrator_8Bits subtrator_8bits_1 (
    .A0(A[0]), .B0(B[0]), .A1(A[1]), .A2(A[2]), .A3(A[3]), .A4(A[4]), .A5(A[5]), .A6(A[6]), .A7(A[7]),
    .B1(B[1]), .B2(B[2]), .B3(B[3]), .B4(B[4]), .B5(B[5]), .B6(B[6]), .B7(B[7]), .S0(\Subtração [0]),
    .S1(\Subtração [1]), .S2(\Subtração [2]), .S3(\Subtração [3]), .S4(\Subtração [4]), .S5(\Subtração [5]),
    .S6(\Subtração [6]), .S7(\Subtração [7]));
  Somador_8bits somador_8bits_1 (
    .A0(A[0]), .B0(B[0]), .A1(A[1]), .A2(A[2]), .A3(A[3]), .A4(A[4]), .A5(A[5]), .A6(A[6]), .A7(A[7]),
    .B1(B[1]), .B2(B[2]), .B3(B[3]), .B4(B[4]), .B5(B[5]), .B6(B[6]), .B7(B[7]), .S0(Soma[0]), .S1(Soma[1]),
    .S2(Soma[2]), .S3(Soma[3]), .S4(Soma[4]), .S5(Soma[5]), .S6(Soma[6]), .S7(Soma[7]));
  multiplicador_8Bits multiplicador_8bits_1 (
    .A0(A[0]), .B0(B[0]), .A1(A[1]), .A2(A[2]), .A3(A[3]), .A4(A[4]), .A5(A[5]), .A6(A[6]), .A7(A[7]),
    .B1(B[1]), .B2(B[2]), .B3(B[3]), .B4(B[4]), .B5(B[5]), .B6(B[6]), .B7(B[7]), .P0(LSB[0]), .P1(LSB[1]),
    .P2(LSB[2]), .P3(LSB[3]), .P4(LSB[4]), .P5(LSB[5]), .P6(LSB[6]), .P7(LSB[7]), .P8(MSB[0]), .P9(MSB[1]),
    .P10(MSB[2]), .P11(MSB[3]), .P12(MSB[4]), .P13(MSB[5]), .P14(MSB[6]), .P15(MSB[7]));
  // divisor_8bits divisor_8bits_1: pin names not known; wires that end beside it: A[0], B[0], A[1], A[2], A[3], A[4], A[5], A[6], A[7], B[1], B[2], B[3], B[4], B[5], B[6], B[7], Resto[0], Quociente[0], Resto[1], Resto[2], Resto[3], Resto[4], Resto[5], Resto[6], Resto[7], Quociente[1], Quociente[2], Quociente[3], Quociente[4], Quociente[5], Quociente[6], Quociente[7]
  Shift_direita shift_direita_1 (
    .A0(A[0]), .A1(A[1]), .A2(A[2]), .A3(A[3]), .A4(A[4]), .A5(A[5]), .A6(A[6]), .A7(A[7]),
    .S0(Shift_direita[0]), .S1(Shift_direita[1]), .S2(Shift_direita[2]), .S3(Shift_direita[3]),
    .S4(Shift_direita[4]), .S5(Shift_direita[5]), .S6(Shift_direita[6]), .S7(Shift_direita[7]));
  Shift_esquerda shift_esquerda_1 (
    .A0(A[0]), .A1(A[1]), .A2(A[2]), .A3(A[3]), .A4(A[4]), .A5(A[5]), .A6(A[6]), .A7(A[7]),
    .S0(Shift_esquerda[0]), .S1(Shift_esquerda[1]), .S2(Shift_esquerda[2]), .S3(Shift_esquerda[3]),
    .S4(Shift_esquerda[4]), .S5(Shift_esquerda[5]), .S6(Shift_esquerda[6]), .S7(Shift_esquerda[7]));
  NAND nand_1 (.A(A), .B(B), .S(NAND));
  XOR_8bits xor_8bits_1 (.A(A), .B(B), .S(XOR));
  Multiplexer #(.Selector_Bits(3), .Bits(8)) multiplexer_1 (
    .sel(Sel___AC), .in_0(Soma), .in_1(\Subtração ), .in_2(LSB), .in_3(Resto), .in_4(Shift_direita),
    .in_5(Shift_esquerda), .in_6(NAND), .in_7(XOR), .out(AC));
  Multiplexer #(.Selector_Bits(2), .Bits(8)) multiplexer_2 (
    .sel(Sel___MQ), .in_0({8{1'b0}}), .in_1(MSB), .in_2(Quociente), .in_3({8{1'b0}}), .out(MQ));
endmodule
