// Digital circuit CPU.dig as structural Verilog
module CPU (
  output [7:0] AC,
  output [7:0] MQ
);

  wire CLK;
  wire [3:0] counter_1_out;
  wire [4:0] OPCODE_d;
  wire [7:0] alu_final_1_ac, alu_final_1_mq, Operandos_d;

  Button button_1 (.out(CLK));
  Counter #(.Bits(4)) counter_1 (.en(1'b1), .C(CLK), .clr(1'b0), .out(counter_1_out));  // open: ovf
  EEPROMDualPort #(.AddrBits(4), .Bits(5), .isProgramMemory("true")) OPCODE (
    .A(counter_1_out), .Din({5{1'b0}}), .str(1'b0), .C(CLK), .ld(1'b1), .D(OPCODE_d));
  EEPROMDualPort #(.AddrBits(4), .Bits(8)) Operandos (
    .A(counter_1_out), .Din({8{1'b0}}), .str(1'b0), .C(CLK), .ld(1'b1), .D(Operandos_d));
  ALU_FINAL alu_final_1 (
    .A(AC), .B(Operandos_d), .Sel___AC(OPCODE_d[4:2]), .Sel___MQ(OPCODE_d[1:0]), .AC(alu_final_1_ac),
    .MQ(alu_final_1_mq));
  Register #(.Bits(8)) u_AC (.D(alu_final_1_ac), .C(CLK), .en(1'b1), .Q(AC));
  Register #(.Bits(8)) u_MQ (.D(alu_final_1_mq), .C(CLK), .en(1'b1), .Q(MQ));

  // Notes on the sheet:
  //   Instruções
  //   Soma 1
  //   Multiplica por 2
  //   soma 3
  //   Subtrai 1
  //   Divide por 3
  //   contents of OPCODE (hex, n*v repeats v):
  //   0,9,0,4,e
  //   contents of Operandos (hex, n*v repeats v):
  //   1,2,3,1,3
  //   Opcode
  //   Soma = 000
  //   Multiplicação - SLB = 010 e MSB = 01
  //   Subtração = 001
  //   Divisão - Quociente = 10 e Resto = 011
endmodule
