// Digital circuit Somador_1Bit.dig as structural Verilog
module Somador_1Bit (
  input  a,
  input  b,
  input  Cin,
  output S,
  output Cout
);

  wire and_1_out, and_2_out, and_3_out, xor_1_out;

  xor xor_1 (xor_1_out, a, b);
  and and_1 (and_1_out, a, b);
  and and_2 (and_2_out, b, Cin);
  and and_3 (and_3_out, a, Cin);
  xor xor_2 (S, xor_1_out, Cin);
  or or_1 (Cout, and_1_out, and_2_out, and_3_out);
endmodule
