// Digital circuit Somador_8bits.dig as structural Verilog
module Somador_8bits (
  input  A0,
  input  B0,
  input  A1,
  input  A2,
  input  A3,
  input  A4,
  input  A5,
  input  A6,
  input  A7,
  input  B1,
  input  B2,
  input  B3,
  input  B4,
  input  B5,
  input  B6,
  input  B7,
  output S0,
  output S1,
  output S2,
  output S3,
  output S4,
  output S5,
  output S6,
  output S7
);

  wire somador_1bit_1_cout, somador_1bit_2_cout, somador_1bit_3_cout, somador_1bit_4_cout,
       somador_1bit_5_cout, somador_1bit_6_cout, somador_1bit_7_cout, somador_1bit_8_cout;

  Somador_1Bit somador_1bit_1 (.a(A0), .b(B0), .Cin(1'b0), .S(S0), .Cout(somador_1bit_1_cout));
  Somador_1Bit somador_1bit_2 (.a(A1), .b(B1), .Cin(somador_1bit_1_cout), .S(S1), .Cout(somador_1bit_2_cout));
  Somador_1Bit somador_1bit_3 (.a(A2), .b(B2), .Cin(somador_1bit_2_cout), .S(S2), .Cout(somador_1bit_3_cout));
  Somador_1Bit somador_1bit_4 (.a(A3), .b(B3), .Cin(somador_1bit_3_cout), .S(S3), .Cout(somador_1bit_4_cout));
  Somador_1Bit somador_1bit_5 (.a(A4), .b(B4), .Cin(somador_1bit_4_cout), .S(S4), .Cout(somador_1bit_5_cout));
  Somador_1Bit somador_1bit_6 (.a(A5), .b(B5), .Cin(somador_1bit_5_cout), .S(S5), .Cout(somador_1bit_6_cout));
  Somador_1Bit somador_1bit_7 (.a(A6), .b(B6), .Cin(somador_1bit_6_cout), .S(S6), .Cout(somador_1bit_7_cout));
  Somador_1Bit somador_1bit_8 (.a(A7), .b(A7), .Cin(somador_1bit_7_cout), .S(S7), .Cout(somador_1bit_8_cout));
  // also tied to GND on the sheet: somador_1bit_8_cout

  // Other names for the same wires on the sheet: A0_t = A0; A2_t = A1; A4_t = A2; A8 = A3; A16 = A4; A32 = A5;
  //   A64 = A6; A128 = A7; B0_t = B0; B2_t = B1; B4_t = B2; B8 = B3; B16 = B4; B32 = B5; B64 = B6; B128 = B7;
  //   S0_t = S0; S2_t = S1; S4_t = S2; S8 = S3; S16 = S4; S32 = S5; S64 = S6; S128 = S7
endmodule
