// Digital circuit Subtrator_1bit.dig as structural Verilog
module Subtrator_1bit (
  input  a,
  input  b,
  input  Cin,
  output S,
  output Cout
);

  wire and_1_out, and_2_out, and_3_out, not_1_out, xor_1_out;

  not not_1 (not_1_out, a);
  xor xor_1 (xor_1_out, a, b);
  and and_1 (and_1_out, not_1_out, b);
  and and_2 (and_2_out, not_1_out, Cin);
  and and_3 (and_3_out, b, Cin);
  xor xor_2 (S, xor_1_out, Cin);
  or or_1 (Cout, and_1_out, and_2_out, and_3_out);
endmodule
