// Digital circuit Subtrator_8Bits.dig as structural Verilog
module Subtrator_8Bits (
  input  A0,
  input  B0,
  input  A1,
  input  A2,
  input  A3,
  input  A4,
  input  A5,
  input  A6,
  input  A7,
  input  B1,
  input  B2,
  input  B3,
  input  B4,
  input  B5,
  input  B6,
  input  B7,
  output S0,
  output S1,
  output S2,
  output S3,
  output S4,
  output S5,
  output S6,
  output S7
);

  wire subtrator_1bit_1_cout, subtrator_1bit_2_cout, subtrator_1bit_3_cout, subtrator_1bit_4_cout,
       subtrator_1bit_5_cout, subtrator_1bit_6_cout, subtrator_1bit_7_cout;

  Subtrator_1bit subtrator_1bit_1 (.a(A0), .b(B0), .Cin(1'b0), .S(S0), .Cout(subtrator_1bit_1_cout));
  Subtrator_1bit subtrator_1bit_2 (.a(A1), .b(B1), .Cin(subtrator_1bit_1_cout), .S(S1), .Cout(subtrator_1bit_2_cout));
  Subtrator_1bit subtrator_1bit_3 (.a(A2), .b(B2), .Cin(subtrator_1bit_2_cout), .S(S2), .Cout(subtrator_1bit_3_cout));
  Subtrator_1bit subtrator_1bit_4 (.a(A3), .b(B3), .Cin(subtrator_1bit_3_cout), .S(S3), .Cout(subtrator_1bit_4_cout));
  Subtrator_1bit subtrator_1bit_5 (.a(A4), .b(B4), .Cin(subtrator_1bit_4_cout), .S(S4), .Cout(subtrator_1bit_5_cout));
  Subtrator_1bit subtrator_1bit_6 (.a(A5), .b(B5), .Cin(subtrator_1bit_5_cout), .S(S5), .Cout(subtrator_1bit_6_cout));
  Subtrator_1bit subtrator_1bit_7 (.a(A6), .b(B6), .Cin(subtrator_1bit_6_cout), .S(S6), .Cout(subtrator_1bit_7_cout));
  Subtrator_1bit subtrator_1bit_8 (.a(A7), .b(B7), .Cin(subtrator_1bit_7_cout), .S(S7));  // open: Cout

  // Other names for the same wires on the sheet: A0_t = A0; A2_t = A1; A4_t = A2; A8 = A3; A16 = A4; A32 = A5;
  //   A64 = A6; A128 = A7; B0_t = B0; B2_t = B1; B4_t = B2; B8 = B3; B16 = B4; B32 = B5; B64 = B6; B128 = B7;
  //   S0_t = S0; S2_t = S1; S4_t = S2; S8 = S3; S16 = S4; S32 = S5; S64 = S6; S128 = S7
endmodule
