// Digital circuit contador.dig as structural Verilog
module contador (
  input  clk
);

  wire and_1_out, and_2_out, and_3_out, and_4_out, B0, B1, button_1_out, jk_ff_as_1_nq, jk_ff_as_2_nq;
  wire [3:0] driver_1_out, register_1_q, register_2_q, register_3_q, register_4_q;

  Button button_1 (.out(button_1_out));
  and and_1 (and_1_out, ~B0, ~B1);  // And
  and and_2 (and_2_out, B0, ~B1);  // And
  and and_3 (and_3_out, ~B0, B1);  // And
  and and_4 (and_4_out, B0, B1);
  JK_FF_AS jk_ff_as_1 (.Set(button_1_out), .J(1'b1), .C(clk), .K(1'b1), .Clr(1'b0), .Q(B0), .nQ(jk_ff_as_1_nq));
  Register #(.Bits(4)) register_1 (.D(4'b0001), .C(clk), .en(1'b1), .Q(register_1_q));
  Register #(.Bits(4)) register_2 (.D(4'b0010), .C(clk), .en(1'b1), .Q(register_2_q));
  Register #(.Bits(4)) register_3 (.D(4'b0011), .C(clk), .en(1'b1), .Q(register_3_q));
  Register #(.Bits(4)) register_4 (.D(4'b0100), .C(clk), .en(1'b1), .Q(register_4_q));
  LED led_1 (.in(B0));
  JK_FF_AS jk_ff_as_2 (.Set(1'b0), .J(1'b1), .C(jk_ff_as_1_nq), .K(1'b1), .Clr(1'b0), .Q(B1), .nQ(jk_ff_as_2_nq));
  assign driver_1_out = and_1_out ? register_1_q : 4'bz;  // Driver driver_1
  assign driver_1_out = and_2_out ? register_2_q : 4'bz;  // Driver driver_2
  assign driver_1_out = and_3_out ? register_3_q : 4'bz;  // Driver driver_3
  assign driver_1_out = and_4_out ? register_4_q : 4'bz;  // Driver driver_4
  LED led_2 (.in(B1));
  Seven_Seg_Hex seven_seg_hex_1 (.d(driver_1_out), .dp(1'b0));
endmodule
