// Digital circuit divisor-8bits.dig as structural Verilog
module divisor_8bits (
  input  A0,
  input  B0,
  input  A1,
  input  A2,
  input  A3,
  input  A4,
  input  A5,
  input  A6,
  input  A7,
  input  B1,
  input  B2,
  input  B3,
  input  B4,
  input  B5,
  input  B6,
  input  B7,
  output [7:0] R0,
  output [7:0] Q0,
  output R1,
  output R2,
  output R3,
  output R4,
  output R5,
  output R6,
  output R7,
  output Q1,
  output Q2,
  output Q3,
  output Q4,
  output Q5,
  output Q6,
  output Q7
);

  wire r0_t_t, r1_t_t, r2_t_t, r3_t_t, r4_t_t, r5_t_t, r6_t_t, r7_t_t, r8, r9, r10, r11, r12, r13, r14, r15,
       r16, r17, r18, r19, r20, r21, r22, r23, r24, r25, r26, r27, r28, r29, r30, r31, r32, r33, r34, r35,
       r36, r37, r38, r39, r40, r41, r42, r43, r44, r45, r46, r47, r48, restore_1_r, restore_2_cout,
       restore_3_r, restore_4_cout, restore_5_cout, restore_6_r, restore_7_cout, restore_8_cout,
       restore_9_cout, restore_10_r, restore_11_cout, restore_12_cout, restore_13_cout, restore_14_cout,
       restore_15_r, restore_16_cout, restore_17_cout, restore_18_cout, restore_19_cout, restore_20_cout,
       restore_21_r, restore_22_cout, restore_23_cout, restore_24_cout, restore_25_r, restore_26_cout,
       restore_27_cout, restore_28_cout, restore_29_cout, restore_30_cout, restore_31_cout, restore_32_cout,
       restore_33_cout, restore_34_cout, restore_35_cout, restore_37_cout, restore_38_cout, restore_39_cout,
       restore_40_cout, restore_41_cout, restore_42_cout, restore_43_cout, restore_44_cout, restore_45_cout,
       restore_46_cout, restore_47_cout, restore_48_cout, restore_49_cout, restore_50_cout, restore_51_cout,
       restore_52_cout, restore_53_cout, restore_54_cout, restore_55_cout, restore_56_cout, restore_57_cout,
       restore_58_cout, restore_59_cout, restore_60_cout, restore_61_cout, restore_62_cout, restore_63_cout,
       restore_64_cout;

  restore restore_1 (.A(1'b0), .B(B7), .Cin(restore_2_cout), .S(Q7), .R(restore_1_r), .Cout(Q7));
  restore restore_2 (.A(1'b0), .B(B6), .Cin(restore_4_cout), .S(Q7), .R(r6_t_t), .Cout(restore_2_cout));
  restore restore_3 (.A(r6_t_t), .B(B7), .Cin(restore_5_cout), .S(Q6), .R(restore_3_r), .Cout(Q6));
  restore restore_4 (.A(1'b0), .B(B5), .Cin(restore_7_cout), .S(Q7), .R(r5_t_t), .Cout(restore_4_cout));
  restore restore_5 (.A(r5_t_t), .B(B6), .Cin(restore_8_cout), .S(Q6), .R(r13), .Cout(restore_5_cout));
  restore restore_6 (.A(r13), .B(B7), .Cin(restore_9_cout), .S(Q5), .R(restore_6_r), .Cout(Q5));
  restore restore_7 (.A(1'b0), .B(B4), .Cin(restore_11_cout), .S(Q7), .R(r4_t_t), .Cout(restore_7_cout));
  restore restore_8 (.A(r4_t_t), .B(B5), .Cin(restore_12_cout), .S(Q6), .R(r12), .Cout(restore_8_cout));
  restore restore_9 (.A(r12), .B(B6), .Cin(restore_13_cout), .S(Q5), .R(r20), .Cout(restore_9_cout));
  restore restore_10 (.A(r20), .B(B7), .Cin(restore_14_cout), .S(Q4), .R(restore_10_r), .Cout(Q4));
  restore restore_11 (.A(1'b0), .B(B3), .Cin(restore_16_cout), .S(Q7), .R(r3_t_t), .Cout(restore_11_cout));
  restore restore_12 (.A(r3_t_t), .B(B4), .Cin(restore_17_cout), .S(Q6), .R(r11), .Cout(restore_12_cout));
  restore restore_13 (.A(r11), .B(B5), .Cin(restore_18_cout), .S(Q5), .R(r19), .Cout(restore_13_cout));
  restore restore_14 (.A(r19), .B(B6), .Cin(restore_19_cout), .S(Q4), .R(r27), .Cout(restore_14_cout));
  restore restore_15 (.A(r27), .B(B7), .Cin(restore_20_cout), .S(Q3), .R(restore_15_r), .Cout(Q3));
  restore restore_16 (.A(1'b0), .B(B2), .Cin(restore_26_cout), .S(Q7), .R(r2_t_t), .Cout(restore_16_cout));
  restore restore_17 (.A(r2_t_t), .B(B3), .Cin(restore_27_cout), .S(Q6), .R(r10), .Cout(restore_17_cout));
  restore restore_18 (.A(r10), .B(B4), .Cin(restore_28_cout), .S(Q5), .R(r18), .Cout(restore_18_cout));
  restore restore_19 (.A(r18), .B(B5), .Cin(restore_22_cout), .S(Q4), .R(r26), .Cout(restore_19_cout));
  restore restore_20 (.A(r26), .B(B6), .Cin(restore_23_cout), .S(Q3), .R(r34), .Cout(restore_20_cout));
  restore restore_21 (.A(r34), .B(B7), .Cin(restore_24_cout), .S(Q2), .R(restore_21_r), .Cout(Q2));
  restore restore_22 (.A(r17), .B(B4), .Cin(restore_32_cout), .S(Q4), .R(r25), .Cout(restore_22_cout));
  restore restore_23 (.A(r25), .B(B5), .Cin(restore_33_cout), .S(Q3), .R(r33), .Cout(restore_23_cout));
  restore restore_24 (.A(r33), .B(B6), .Cin(restore_34_cout), .S(Q2), .R(r41), .Cout(restore_24_cout));
  restore restore_25 (.A(r41), .B(B7), .Cin(restore_35_cout), .S(Q1), .R(restore_25_r), .Cout(Q1));
  restore restore_26 (.A(1'b0), .B(B1), .Cin(restore_29_cout), .S(Q7), .R(r1_t_t), .Cout(restore_26_cout));
  restore restore_27 (.A(r1_t_t), .B(B2), .Cin(restore_30_cout), .S(Q6), .R(r9), .Cout(restore_27_cout));
  restore restore_28 (.A(r9), .B(B3), .Cin(restore_31_cout), .S(Q5), .R(r17), .Cout(restore_28_cout));
  restore restore_29 (.A(A7), .B(B0), .Cin(1'b1), .S(Q7), .R(r0_t_t), .Cout(restore_29_cout));
  restore restore_30 (.A(r0_t_t), .B(B1), .Cin(restore_37_cout), .S(Q6), .R(r8), .Cout(restore_30_cout));
  restore restore_31 (.A(r8), .B(B2), .Cin(restore_38_cout), .S(Q5), .R(r16), .Cout(restore_31_cout));
  restore restore_32 (.A(r16), .B(B3), .Cin(restore_39_cout), .S(Q4), .R(r24), .Cout(restore_32_cout));
  restore restore_33 (.A(r24), .B(B4), .Cin(restore_40_cout), .S(Q3), .R(r32), .Cout(restore_33_cout));
  restore restore_34 (.A(r32), .B(B5), .Cin(restore_41_cout), .S(Q2), .R(r40), .Cout(restore_34_cout));
  restore restore_35 (.A(r40), .B(B6), .Cin(restore_42_cout), .S(Q1), .R(r48), .Cout(restore_35_cout));
  restore restore_36 (.A(r48), .B(B7), .Cin(restore_43_cout), .S(Q1), .R(R7), .Cout(Q0[0]));
  restore restore_37 (.A(A6), .B(B0), .Cin(1'b1), .S(Q6), .R(r7_t_t), .Cout(restore_37_cout));
  restore restore_38 (.A(r7_t_t), .B(B1), .Cin(restore_44_cout), .S(Q5), .R(r15), .Cout(restore_38_cout));
  restore restore_39 (.A(r15), .B(B2), .Cin(restore_45_cout), .S(Q4), .R(r23), .Cout(restore_39_cout));
  restore restore_40 (.A(r23), .B(B3), .Cin(restore_46_cout), .S(Q3), .R(r31), .Cout(restore_40_cout));
  restore restore_41 (.A(r31), .B(B4), .Cin(restore_47_cout), .S(Q2), .R(r39), .Cout(restore_41_cout));
  restore restore_42 (.A(r39), .B(B5), .Cin(restore_48_cout), .S(Q1), .R(r47), .Cout(restore_42_cout));
  restore restore_43 (.A(r47), .B(B6), .Cin(restore_49_cout), .S(Q0[0]), .R(R6), .Cout(restore_43_cout));
  restore restore_44 (.A(A5), .B(B0), .Cin(1'b1), .S(Q5), .R(r14), .Cout(restore_44_cout));
  restore restore_45 (.A(r14), .B(B1), .Cin(restore_51_cout), .S(Q4), .R(r22), .Cout(restore_45_cout));
  restore restore_46 (.A(r22), .B(B2), .Cin(restore_52_cout), .S(Q3), .R(r30), .Cout(restore_46_cout));
  restore restore_47 (.A(r30), .B(B3), .Cin(restore_53_cout), .S(Q2), .R(r38), .Cout(restore_47_cout));
  restore restore_48 (.A(r38), .B(B4), .Cin(restore_54_cout), .S(Q1), .R(r46), .Cout(restore_48_cout));
  restore restore_49 (.A(r46), .B(B5), .Cin(restore_50_cout), .S(Q0[0]), .R(R5), .Cout(restore_49_cout));
  restore restore_50 (.A(r45), .B(B4), .Cin(restore_58_cout), .S(Q0[0]), .R(R4), .Cout(restore_50_cout));
  restore restore_51 (.A(A4), .B(B0), .Cin(1'b1), .S(Q4), .R(r21), .Cout(restore_51_cout));
  restore restore_52 (.A(r21), .B(B1), .Cin(restore_55_cout), .S(Q3), .R(r29), .Cout(restore_52_cout));
  restore restore_53 (.A(r29), .B(B2), .Cin(restore_56_cout), .S(Q2), .R(r37), .Cout(restore_53_cout));
  restore restore_54 (.A(r37), .B(B3), .Cin(restore_57_cout), .S(Q1), .R(r45), .Cout(restore_54_cout));
  restore restore_55 (.A(A3), .B(B0), .Cin(1'b1), .S(Q3), .R(r28), .Cout(restore_55_cout));
  restore restore_56 (.A(r28), .B(B1), .Cin(restore_59_cout), .S(Q2), .R(r36), .Cout(restore_56_cout));
  restore restore_57 (.A(r36), .B(B2), .Cin(restore_60_cout), .S(Q1), .R(r44), .Cout(restore_57_cout));
  restore restore_58 (.A(r44), .B(B3), .Cin(restore_61_cout), .S(Q0[0]), .R(R3), .Cout(restore_58_cout));
  restore restore_59 (.A(A2), .B(B0), .Cin(1'b1), .S(Q2), .R(r35), .Cout(restore_59_cout));
  restore restore_60 (.A(r35), .B(B1), .Cin(restore_62_cout), .S(Q1), .R(r43), .Cout(restore_60_cout));
  restore restore_61 (.A(r43), .B(B2), .Cin(restore_63_cout), .S(Q0[0]), .R(R2), .Cout(restore_61_cout));
  restore restore_62 (.A(A1), .B(B0), .Cin(1'b1), .S(Q1), .R(r42), .Cout(restore_62_cout));
  restore restore_63 (.A(r42), .B(B1), .Cin(restore_64_cout), .S(Q0[0]), .R(R1), .Cout(restore_63_cout));
  restore restore_64 (.A(A0), .B(B0), .Cin(1'b1), .S(Q0[0]), .R(R0[0]), .Cout(restore_64_cout));
  // Pins of 1 and 8 bits meet at R0
  // Pins of 1 and 8 bits meet at Q0
  // also tied to GND on the sheet: {restore_1_r, restore_3_r, restore_6_r, restore_10_r, restore_15_r, restore_21_r, restore_25_r}

  // Other names for the same wires on the sheet: D0 = A0; D1 = A1; D2 = A2; D3 = A3; D4 = A4; D5 = A5; D6 = A6;
  //   D7 = A7; d0_t = B0; d1_t = B1; d2_t = B2; d3_t = B3; d4_t = B4; d5_t = B5; d6_t = B6; d7_t = B7; Cout7 = Q0[0];
  //   Q0_t = Q0[0]; Cout6 = Q1; Q1_t = Q1; Cout5 = Q2; Q2_t = Q2; Cout4 = Q3; Q3_t = Q3; Cout3 = Q4; Q4_t = Q4;
  //   Cout2 = Q5; Q5_t = Q5; Cout1 = Q6; Q6_t = Q6; Cout0 = Q7; Q7_t = Q7; R0_t = R0[0]; R1_t = R1; R2_t = R2;
  //   R3_t = R3; R4_t = R4; R5_t = R5; R6_t = R6; R7_t = R7
endmodule
