// Digital circuit full-adder.dig as structural Verilog
module full_adder (
  input  a,
  input  b,
  input  Cin,
  output S,
  output Cout
);

  wire and_1_out, and_2_out, and_3_out, xor_1_s, xor_3_s;

  XOR xor_1 (.A(a), .B(b), .S(xor_1_s));
  and and_1 (and_1_out, a, b);
  and and_2 (and_2_out, b, Cin);
  and and_3 (and_3_out, a, Cin);
  XOR xor_2 (.A(xor_1_s), .B(Cin), .S(S));
  XOR xor_3 (.A(and_1_out), .B(and_2_out), .S(xor_3_s));
  XOR xor_4 (.A(xor_3_s), .B(and_3_out), .S(Cout));
endmodule
