// Digital circuit restore.dig as structural Verilog
module restore (
  input  A,
  input  B,
  input  Cin,
  input  S,
  output R,
  output Cout
);

  wire tBnot, tSub;

  not not_1 (tBnot, B);
  Multiplexer multiplexer_1 (.sel(S), .in_0(A), .in_1(tSub), .out(R));
  full_adder full_adder_1 (.a(A), .b(tBnot), .Cin(Cin), .S(tSub), .Cout(Cout));

  // Other names for the same wires on the sheet: tA = A; tCin = Cin; tCout = Cout
endmodule
