// Digital circuit half-adder.dig as structural Verilog
module half_adder (
  input  A,
  input  B,
  output S,
  output Cout
);

  XOR xor_1 (.A(A), .B(B), .S(S));
  and and_1 (Cout, A, B);
endmodule
